# Fritzing sketch yetos_air (saved by Fritzing 0.9.3b)

parts:
  Part2 = Arduino Uno (Rev3) - ICSP  # not connected
  Part4 = Barometric Pressure Sensor - BMP085 Breakout
  Part5 = Arduino Board Ethernet

nets:
  VCC: Part4.VCC, Part5.3V3
  GND: Part4.GND, Part5.GND
  N1: Part4.SCL, Part5.A5
  N2: Part4.SDA, Part5.A4
